# Fritzing sketch nodemcu_temperature_reading (saved by Fritzing 0.9.3b)
breadboards: 2

parts:
  U1 = NodeMCU V3.0
  DS1 = DS18B20 1-Wire Temperature Sensor [part_number=DS18B20]
  R1 = Resistor [tolerance=±5% resistance=4.7k package="1206 [SMD]"]
  R2 = Resistor [tolerance=±5% resistance=220 package=THT]
  LED1 = smd LED [color="Red (633nm)" package="0805 [SMD]"]

nets:
  N1: U1.GND#16, U1.GND#33
  N2: DS1.GND, LED1.cathode
  N3: DS1.DQ, R1.Pin_0
  N4: DS1.VDD, R1.Pin_1
  N5: R2.Pin_1, LED1.anode

custom parts:
  NodeMCU V3.0: ESP8266 based NodeMCU
